# Fritzing sketch eeprom-programmer-breadboard (saved by Fritzing 0.9.1b)
circuit board: 16.9333cm x 5.64444cm
breadboards: 1

parts:
  U1 = MCP 23017 [chip_label=23017 package=THT]
  U2 = MCP 23017 [chip_label=23017 package=THT]
  28c65 = mystery part, 28 pins [chip_label="28c65 or 28c256"]
  Arduino_Ethernet_Shield1 = Arduino Ethernet Shield (Rev3)

nets:
  N1: U1.pin1, 28c65.pin10
  N2: U1.pin2, 28c65.pin9
  N3: U1.pin3, 28c65.pin8
  N4: U1.pin4, 28c65.pin7
  N5: U1.pin5, 28c65.pin6
  N6: U1.pin6, 28c65.pin5
  N7: U1.pin7, 28c65.pin4
  N8: U1.pin8, 28c65.pin3
  N9: U1.pin9, U1.pin18, U2.pin9, U2.pin15, U2.pin18, 28c65.pin28
  N10: U1.pin10, U1.pin15, U1.pin16, U1.pin17, U2.pin10, U2.pin16, U2.pin17, 28c65.pin14, Arduino_Ethernet_Shield1.GND
  N11: U1.pin12, U2.pin12
  N12: U1.pin13, U2.pin13
  N13: U1.pin21, 28c65.pin25
  N14: U1.pin22, 28c65.pin24
  N15: U1.pin23, 28c65.pin21
  N16: U1.pin24, 28c65.pin23
  N17: U1.pin25, 28c65.pin2
  N18: U1.pin26, 28c65.pin26
  N19: U1.pin27, 28c65.pin1
  N20: U2.pin1, 28c65.pin11
  N21: U2.pin2, 28c65.pin12
  N22: U2.pin3, 28c65.pin13
  N23: U2.pin4, 28c65.pin15
  N24: U2.pin5, 28c65.pin16
  N25: U2.pin6, 28c65.pin17
  N26: U2.pin7, 28c65.pin18
  N27: U2.pin8, 28c65.pin19
  N28: U2.pin21, 28c65.pin20
  N29: U2.pin22, 28c65.pin22
  N30: U2.pin23, 28c65.pin27

custom parts:
  MCP 23017: A dummy, proxy, ersatz, stand-in part for whatever you want. With 28 pins on a 300mil inline pin header footprint.
